// Logisim project Q2 circuit.circ as structural Verilog: 1 circuit, main circuit main
module main (
  input  in_1,
  input  A,
  input  D
);

  wire A_AND_C_out, A_AND_D_out, A_OR_C_out, and_1_out, and_2_out, not_1_out, or_1_out, or_2_out;

  and A_AND_C (A_AND_C_out, in_1, A);
  or A_OR_C (A_OR_C_out, in_1, A);
  and A_AND_D (A_AND_D_out, A, D);
  not not_1 (not_1_out, D);
  and and_1 (and_1_out, A, not_1_out);
  or or_1 (or_1_out, A_AND_D_out, and_1_out);
  and and_2 (and_2_out, A_OR_C_out, or_1_out);
  or or_2 (or_2_out, A_AND_C_out, in_1, and_2_out);
  LED led_1 (.in(or_2_out));

  // Notes on the sheet:
  //   C
  //   1
  //   4
  //   3
  //   2
  //   A AND D'
  //   5
  //   (A AND D) OR (A AND D' )
  //   6
  //   7
  //   ((A AND D) OR (A AND D' )) AND (A OR C)
endmodule
