// Logisim project Assignment 4 - Circuit.circ as structural Verilog: 1 circuit, main circuit main
module main (
  input  X,
  input  Y,
  input  Z
);

  wire and_1_out, and_2_out, and_3_out, and_4_out, and_5_out, not_1_out, not_2_out;

  and and_1 (and_1_out, Y, Z);
  and and_2 (and_2_out, Z, X);
  and and_3 (and_3_out, X, Y, Z);
  not not_1 (not_1_out, and_1_out);
  not not_2 (not_2_out, and_2_out);
  LED led_1 (.in(and_3_out));
  LED led_2 (.in(and_4_out));
  and and_4 (and_4_out, X, not_1_out);
  and and_5 (and_5_out, Y, not_2_out);
  LED led_3 (.in(and_5_out));

  // Notes on the sheet:
  //   A = XYZ
  //   B = X ( YZ )'
  //   C = Y ( XZ ) '
endmodule
