// Logisim project circuit.circ as structural Verilog: 1 circuit, main circuit main
module main (
  input  in_1,
  input  in_2,
  input  in_3,
  input  in_4
);

  wire and_1_out, and_2_out, clock_1_out, d_ff_1_q, d_ff_1_qn, j_k_ff_1_q, multiplexer_1_out, nand_1_out,
       not_1_out, or_1_out;

  not not_1 (not_1_out, in_1);
  and and_1 (and_1_out, d_ff_1_q, not_1_out);
  and and_2 (and_2_out, not_1_out, j_k_ff_1_q);
  nand nand_1 (nand_1_out, d_ff_1_q, j_k_ff_1_q);
  Clock clock_1 (.out(clock_1_out));
  or or_1 (or_1_out, and_1_out, and_2_out);
  Multiplexer multiplexer_1 (.in0(d_ff_1_qn), .in1(nand_1_out), .out(multiplexer_1_out), .sel(in_1), .en(in_4));
  D_Flip_Flop d_ff_1 (
    .clk(clock_1_out), .D(or_1_out), .Q(d_ff_1_q), .Qn(d_ff_1_qn), .preset(in_2), .en(in_4), .reset(in_3));
  J_K_Flip_Flop j_k_ff_1 (
    .J(multiplexer_1_out), .clk(clock_1_out), .K(in_1), .Q(j_k_ff_1_q), .preset(in_2), .en(in_4), .reset(in_3));  // open: Qn
  LED led_1 (.in(j_k_ff_1_q));
  LED led_2 (.in(d_ff_1_q));
endmodule
