// Logisim project Lab1_COMP 206.circ as structural Verilog: 1 circuit, main circuit main
module main (
  input  in_1,
  input  in_2,
  input  in_3,
  input  in_4,
  input  in_5,
  input  in_6,
  input  in_7,
  input  in_8,
  input  in_9,
  input  in_10,
  input  in_11
);

  wire and_1_out, nand_1_out, nor_1_out, not_1_out, or_1_out, xor_1_out;

  and and_1 (and_1_out, in_1, in_3);
  not not_1 (not_1_out, in_10);
  nand nand_1 (nand_1_out, in_6, in_8);
  LED led_1 (.in(and_1_out));
  LED led_2 (.in(nand_1_out));
  LED led_3 (.in(not_1_out));
  or or_1 (or_1_out, in_2, in_4);
  nor nor_1 (nor_1_out, in_5, in_7);
  xor xor_1 (xor_1_out, in_9, in_11);
  LED led_4 (.in(or_1_out));
  LED led_5 (.in(nor_1_out));
  LED led_6 (.in(xor_1_out));
endmodule
