// Logisim project Lab_2 Ciruit.circ as structural Verilog: 1 circuit, main circuit main
module main (
  input  in_1,
  input  in_2,
  input  in_3,
  input  in_4,
  input  in_5,
  input  in_6,
  input  in_7,
  input  in_8,
  input  in_9,
  input  in_10
);

  wire nand_1_out, nand_2_out, nand_3_out, nand_4_out, nand_5_out, nand_6_out, nor_1_out, nor_2_out,
       nor_3_out, nor_4_out, nor_5_out, nor_6_out;

  nand nand_1 (nand_1_out, in_1, in_1);
  nand nand_2 (nand_2_out, in_3, in_5);
  nand nand_3 (nand_3_out, in_7, in_7);
  nand nand_4 (nand_4_out, in_10, in_10);
  LED led_1 (.in(nand_1_out));
  nand nand_5 (nand_5_out, nand_2_out, nand_2_out);
  LED led_2 (.in(nand_5_out));
  LED led_3 (.in(nand_6_out));
  nand nand_6 (nand_6_out, nand_3_out, nand_4_out);
  nor nor_1 (nor_1_out, in_2, in_2);
  LED led_4 (.in(nor_1_out));
  nor nor_2 (nor_2_out, in_4, in_6);
  nor nor_3 (nor_3_out, in_8, in_8);
  nor nor_4 (nor_4_out, in_9, in_9);
  nor nor_5 (nor_5_out, nor_2_out, nor_2_out);
  LED led_5 (.in(nor_5_out));
  nor nor_6 (nor_6_out, nor_3_out, nor_4_out);
  LED led_6 (.in(nor_6_out));
endmodule
