// Logisim project 231488347_LAB3 - Circuit.circ as structural Verilog: 1 circuit, main circuit main
module main (
  input  X,
  input  X_2,
  input  Y,
  input  Y_2,
  input  Z,
  input  X_3,
  input  Y_3
);

  wire and_1_out, and_2_out, and_3_out, not_1_out, not_2_out, not_3_out, not_4_out, not_5_out, not_6_out,
       not_7_out, or_1_out, or_2_out, or_3_out;

  not not_1 (not_1_out, Y_2);
  not not_2 (not_2_out, Y_3);
  not not_3 (not_3_out, X_3);
  and and_1 (and_1_out, not_1_out, Z);
  or or_1 (or_1_out, X_3, Y_3);
  LED led_1 (.in(or_2_out));
  or or_2 (or_2_out, X, and_1_out);
  not not_4 (not_4_out, or_1_out);
  and and_2 (and_2_out, not_2_out, not_3_out);
  LED led_2 (.in(and_2_out));
  LED led_3 (.in(not_4_out));
  not not_5 (not_5_out, X_2);
  not not_6 (not_6_out, Y);
  and and_3 (and_3_out, X_2, Y);
  or or_3 (or_3_out, not_5_out, not_6_out);
  not not_7 (not_7_out, and_3_out);
  LED led_4 (.in(not_7_out));
  LED led_5 (.in(or_3_out));

  // Notes on the sheet:
  //   Part 1
  //   Part 2 
  //   Theorem 1
  //   F1
  //   X ' Y '
  //   ( X + Y ) '
  //   Theorem 2
  //   ( XY ) '
  //   X ' + Y '
endmodule
