// Logisim project lab5 circuit.circ as structural Verilog: 1 circuit, main circuit main
module main (
  input  A,
  input  B,
  input  A_2,
  input  B_2
);

  wire A_prime___AB_out, AB__prime_out, B_prime___AB_out, nand_1_out, nand_2_out, nand_3_out, nand_4_out,
       nand_5_out, nand_6_out, nand_7_out;

  nand AB__prime (AB__prime_out, A_2, B_2);
  nand nand_1 (nand_1_out, A, 1'b1);
  nand nand_2 (nand_2_out, 1'b1, B);
  nand A_prime___AB (A_prime___AB_out, A_2, AB__prime_out);
  nand B_prime___AB (B_prime___AB_out, AB__prime_out, B_2);
  nand nand_3 (nand_3_out, nand_1_out, B);
  nand nand_4 (nand_4_out, A, nand_2_out);
  nand nand_5 (nand_5_out, A_prime___AB_out, B_prime___AB_out);
  nand nand_6 (nand_6_out, nand_5_out, nand_5_out);
  LED led_1 (.in(nand_6_out));
  LED led_2 (.in(nand_7_out));
  nand nand_7 (nand_7_out, nand_3_out, nand_4_out);

  // Notes on the sheet:
  //   PART 1
  //   PART 2
  //   A'
  //   B'
  //   B
  //   A
  //   A(A'+B') + B(A'+B')
  //   ( A'B )'
  //   ( A'B )'
  //   F = (A'B + AB')
  //   F = A' B' +AB
endmodule
